# Fritzing sketch MusicPlayer (saved by Fritzing 0.9.3b)

parts:
  DFRobot_DFPlayer_Mini1 = DFRobot DFPlayer Mini [part_number=DFR0299]
  Part1 = Arduino Nano (Rev3.0)
  Prev_/_Vol- = Pushbutton [package="[SMD]"]
  Next_/_Vol+ = Pushbutton [package="[SMD]"]
  R1 = Resistor [tolerance=±5% resistance=1k package="0805 [SMD]"]
  8Ω_0_5W = SPEAKER [package=pcb_mount_speaker]
  R2 = Resistor [tolerance=±5% resistance=220 package="0805 [SMD]"]
  Busy_LED_(active_LOW) = smd LED [color="Red (633nm)" package="0805 [SMD]"]
  Start_/_Pause = Pushbutton [package="[SMD]"]

nets:
  VCC: DFRobot_DFPlayer_Mini1.VCC, Part1.5V, Busy_LED_(active_LOW).anode
  N1: DFRobot_DFPlayer_Mini1.RX, R1.Pin_1
  N2: DFRobot_DFPlayer_Mini1.TX, Part1.D10
  N3: DFRobot_DFPlayer_Mini1.SPK_1, 8Ω_0_5W.-
  N4: DFRobot_DFPlayer_Mini1.GND-1, DFRobot_DFPlayer_Mini1.GND-2, Part1.GND, Prev_/_Vol-.Pin_1, Prev_/_Vol-.Pin_2, Next_/_Vol+.Pin_3, Next_/_Vol+.Pin_4, Start_/_Pause.Pin_3
  N5: DFRobot_DFPlayer_Mini1.SPK_2, 8Ω_0_5W.+
  N6: DFRobot_DFPlayer_Mini1.IO_1, Prev_/_Vol-.Pin_3, Prev_/_Vol-.Pin_4
  N7: DFRobot_DFPlayer_Mini1.IO_2, Next_/_Vol+.Pin_1
  N8: DFRobot_DFPlayer_Mini1.BUSY, R2.Pin_1
  N9: Part1.D2, Start_/_Pause.Pin_1, Start_/_Pause.Pin_2
  N10: Part1.D11/MOSI, R1.Pin_0
  N11: R2.Pin_0, Busy_LED_(active_LOW).cathode
